# Fritzing sketch Sketch (saved by Fritzing 0.6.3b)
breadboards: 1

parts:
  Arduino1 = Arduino
  R1 = Resistor [tolerance=±5% resistance=10k package=THT]
  Part1 = ADXL345-BreakoutBoard-v13.fzp

nets:
  N1: Arduino1.3V3, R1.Pin_0, Part1.connector14
  N2: Arduino1.GND, Part1.connector13
  N3: Arduino1.A0, Part1.connector10
  N4: Arduino1.A1, Part1.connector11
  N5: Arduino1.A2, Part1.connector12
  N6: R1.Pin_1, Part1.connector9
